# Fritzing sketch fritzing_guitarHero (saved by Fritzing 0.9.3b)
circuit board: 8.46667cm x 5.64444cm
breadboards: 1

parts:
  Arduino_Micro = Arduino Micro (Rev3)
  LED1 = smd LED [color="Red (635nm)" package="1206 [SMD]"]
  LED2 = smd LED [color="Green (555nm)" package="0805 [SMD]"]
  LED3 = smd LED [color="Blue (505nm)" package="0805 [SMD]"]
  LED4 = smd LED [color="Yellow (585nm)" package="0805 [SMD]"]
  R1 = Resistor [tolerance=±5% resistance=220 package="2512 [SMD]"]
  Push_Button = Pushbutton [package="[SMD]"]
  Potentiometer = Rotary Potentiometer (Small) [maximum_resistance=100kΩ package=THT]

nets:
  N1: Arduino_Micro.GND, LED1.anode, LED2.anode, LED4.anode, R1.Pin_0, Push_Button.Pin_3, Push_Button.Pin_4, Potentiometer.leg1
  N2: Arduino_Micro.D3/SCL, LED4.cathode
  N3: Arduino_Micro.D6_PWM/A7, LED3.cathode
  N4: Arduino_Micro.D7, Push_Button.Pin_1, Push_Button.Pin_2
  N5: Arduino_Micro.D9_PWM/A9, LED2.cathode
  N6: Arduino_Micro.D12_PWM/A11, LED1.cathode
  N7: Arduino_Micro.5V, Potentiometer.leg2
  N8: Arduino_Micro.A0, Potentiometer.wiper
  N9: LED3.anode, R1.Pin_1

// code stored in the sketch: seriale_arduino.ino
const int pin_potenziometro = A0;
const int pin_LEDR = 12;
const int pin_LEDG = 9;
const int pin_LEDB = 6;
const int pin_LEDY = 3;
const int pin_button = 7;


int analog_pot;   // valore potenziometro letto (0 : 1023)
int pos;          // posizione pallina da inviare nella seriale
int pos_prec;     // posizione inviata precedentemente 
int pin_LED;
int data_received;
volatile bool button_flag = LOW;

void setup() {
  Serial.begin(9600);
  
  pinMode(pin_LEDR, OUTPUT);
  pinMode(pin_LEDG, OUTPUT);
  pinMode(pin_LEDB, OUTPUT);
  pinMode(pin_LEDY, OUTPUT);
  pinMode(pin_button, INPUT_PULLUP);

  attachInterrupt(digitalPinToInterrupt(pin_button), setButtonFlag , FALLING);

}

void loop() {

  analog_pot = analogRead(pin_potenziometro);
  
  if(analog_pot >= 0 && analog_pot < 60)     pos = 0;
  if(analog_pot >= 64 && analog_pot < 276)   pos = 1;
  if(analog_pot >= 280 && analog_pot < 648)  pos = 2;
  if(analog_pot >= 652 && analog_pot < 1023) pos = 3;
  
  if(pos != pos_prec) {
     Serial.write(pos);
     pos_prec = pos;
    }

  if(button_flag == HIGH) {
    Serial.write(4);
    button_flag = LOW;
   }

   if(Serial.available()>0){
    data_received = Serial.read();
      if(data_received == 0){
        digitalWrite(pin_LEDR, HIGH);        
        delay(200);
        digitalWrite(pin_LEDR, LOW);
        }
        
      if(data_received == 1){
        digitalWrite(pin_LEDG, HIGH);        
        delay(200);
        digitalWrite(pin_LEDG, LOW);
        }
      if(data_received == 2){
        digitalWrite(pin_LEDB, HIGH);        
        delay(200);
        digitalWrite(pin_LEDB, LOW);
        }
      if(data_received == 3){
        digitalWrite(pin_LEDY, HIGH);        
        delay(200);
        digitalWrite(pin_LEDY, LOW);
      }
    }


delay(1);
}

void setButtonFlag(){
  button_flag = HIGH;
  }
